// Logisim project 2 into 1 mux multibit.circ as structural Verilog: 2 circuits, main circuit main
module _2_to_1_multi (
  input  [3:0] in_1,
  input  [3:0] in_2,
  input  in_3,
  output [3:0] out_4
);

  main main_1 (.out_4(out_4), .in_1(in_1), .in_2(in_2), .in_3(in_3));
endmodule

module main (
  input  [3:0] in_1,
  input  [3:0] in_2,
  input  in_3,
  output [3:0] out_4
);

  Multiplexer multiplexer_1 (.in0(in_1[0]), .in1(in_2[0]), .out(out_4[0]), .sel(in_3));  // open: en
  Multiplexer multiplexer_2 (.in0(in_1[1]), .in1(in_2[1]), .out(out_4[1]), .sel(in_3));  // open: en
  Multiplexer multiplexer_3 (.in0(in_1[2]), .in1(in_2[2]), .out(out_4[2]), .sel(in_3));  // open: en
  Multiplexer multiplexer_4 (.in0(in_1[3]), .in1(in_2[3]), .out(out_4[3]), .sel(in_3));  // open: en
endmodule
