// Logisim project FA and HA.circ as structural Verilog: 1 circuit, main circuit main
module main (
  input  A,
  input  B,
  input  C,
  input  A_2,
  input  B_2,
  output S,
  output C_2,
  output S_2,
  output C_3
);

  wire and_1_out, and_2_out, xor_1_out;

  xor xor_1 (xor_1_out, A, B);
  xor xor_2 (S_2, A_2, B_2);
  and and_1 (and_1_out, A, B);
  and and_2 (and_2_out, xor_1_out, C);
  and and_3 (C_3, A_2, B_2);
  xor xor_3 (S, xor_1_out, C);
  or or_1 (C_2, and_1_out, and_2_out);

  // Notes on the sheet:
  //   HALF ADDER
  //   FULL ADDER
endmodule
