// Logisim project HA AND FA USING 4 INTO 1 MUX.circ as structural Verilog: 1 circuit, main circuit main
module main (
  input  in_1,
  input  in_2,
  input  [1:0] in_3,
  input  in_4,
  output s,
  output c
);

  wire not_1_out;

  not not_1 (not_1_out, in_1);
  Multiplexer #(.select(2)) multiplexer_1 (
    .in0(in_1), .in1(not_1_out), .in2(not_1_out), .in3(in_1), .out(s), .sel(in_3), .en(in_2));
  Multiplexer #(.select(2)) multiplexer_2 (
    .in0(in_1), .in1(in_1), .in2(in_1), .in3(not_1_out), .out(c), .sel(in_3), .en(in_4));

  // Notes on the sheet:
  //   HALF ADDER  AND FULL ADDER USING 4 INTO 1 MUX
endmodule
