// Logisim project HS and FS 2.circ as structural Verilog: 1 circuit, main circuit main
module main (
  input  A,
  input  B,
  input  C,
  input  A_2,
  input  B_2,
  output D,
  output B_3,
  output D_2,
  output B_4
);

  wire and_1_out, and_3_out, not_1_out, not_2_out, xor_1_out;

  not not_1 (not_1_out, A);
  xor xor_1 (xor_1_out, A, B);
  not not_2 (not_2_out, xor_1_out);
  or or_1 (D_2, A_2, B_2);
  xor xor_2 (D, xor_1_out, C);
  and and_1 (and_1_out, not_1_out, B);
  and and_2 (B_4, A_2, B_2);
  and and_3 (and_3_out, not_2_out, C);
  or or_2 (B_3, and_1_out, and_3_out);

  // Notes on the sheet:
  //   FULL SUBTRACTOR
  //   HALF SUBTRACTOR
endmodule
