// Logisim project HS and FS.circ as structural Verilog: 1 circuit, main circuit main
module main (
  input  in_1,
  input  in_2,
  input  in_3,
  input  in_4,
  input  in_5
);

  wire and_1_out, and_2_out, and_3_out, not_1_out, not_2_out, not_3_out, or_1_out, xor_1_out, xor_2_out,
       xor_3_out;

  not not_1 (not_1_out, in_3);
  not not_2 (not_2_out, in_1);
  and and_1 (and_1_out, not_1_out, in_4);
  xor xor_1 (xor_1_out, in_3, in_4);
  not not_3 (not_3_out, xor_1_out);
  xor xor_2 (xor_2_out, in_1, in_2);
  and and_2 (and_2_out, not_2_out, in_2);
  xor xor_3 (xor_3_out, xor_1_out, in_5);
  LED led_1 (.in(xor_3_out));
  and and_3 (and_3_out, not_3_out, in_5);
  or or_1 (or_1_out, and_3_out, and_1_out);
  LED led_2 (.in(and_2_out));
  LED led_3 (.in(or_1_out));
  LED led_4 (.in(xor_2_out));

  // Notes on the sheet:
  //   Half Subtractor
  //   Full Subtractor
endmodule
