// Logisim project Half adder using mux.circ as structural Verilog: 1 circuit, main circuit main
module main (
  input  in_1,
  input  Enable,
  input  [1:0] A_B,
  input  Enable_2,
  input  [1:0] A_B_2,
  output Sum,
  output Carry
);

  wire not_1_out;

  not not_1 (not_1_out, in_1);
  Multiplexer #(.select(2)) multiplexer_1 (
    .in0(in_1), .in1(not_1_out), .in2(not_1_out), .in3(in_1), .out(Sum), .sel(A_B), .en(Enable));
  Multiplexer #(.select(2)) multiplexer_2 (
    .in0(in_1), .in1(in_1), .in2(in_1), .in3(not_1_out), .out(Carry), .sel(A_B_2), .en(Enable_2));
endmodule
