// Logisim project Half subtractor.circ as structural Verilog: 1 circuit, main circuit main
module main (
  input  A,
  input  B,
  input  C,
  output Sum,
  output Borrow
);

  wire and_1_out, and_2_out, not_1_out, not_2_out, xor_1_out;

  xor xor_1 (xor_1_out, A, B);
  not not_1 (not_1_out, A);
  not not_2 (not_2_out, xor_1_out);
  and and_1 (and_1_out, not_2_out, C);
  and and_2 (and_2_out, not_1_out, B);
  xor xor_2 (Sum, xor_1_out, C);
  or or_1 (Borrow, and_1_out, and_2_out);
endmodule
