// Logisim project 4 INTO 1 MUX.circ as structural Verilog: 1 circuit, main circuit main
module main (
  input  in_1,
  input  in_2,
  input  in_3,
  input  in_4,
  input  in_5,
  input  in_6,
  output Y
);

  wire and_1_out, and_2_out, and_3_out, and_4_out, not_1_out, not_2_out;

  not not_1 (not_1_out, in_1);
  not not_2 (not_2_out, in_2);
  and and_1 (and_1_out, not_1_out, not_2_out, in_3);
  and and_2 (and_2_out, not_1_out, in_2, in_4);
  and and_3 (and_3_out, in_1, not_2_out, in_5);
  and and_4 (and_4_out, in_1, in_1, in_6);
  or or_1 (Y, and_1_out, and_2_out, and_3_out, and_4_out);

  // Notes on the sheet:
  //   S0
  //   S1
  //   S0
  //   S!
  //   S2
  //   S3
  //   4 INTO 1 MUX
endmodule
