// Logisim project full subtracter.circ as structural Verilog: 1 circuit, main circuit main
module main (
  input  A,
  input  B,
  input  C,
  output Diffrence,
  output out_5
);

  wire and_1_out, and_2_out, not_1_out, not_2_out, xor_1_out;

  not not_1 (not_1_out, A);
  xor xor_1 (xor_1_out, A, B);
  and and_1 (and_1_out, B, not_1_out);
  xor xor_2 (Diffrence, xor_1_out, C);
  not not_2 (not_2_out, xor_1_out);
  and and_2 (and_2_out, C, not_2_out);
  or or_1 (out_5, and_2_out, and_1_out);

  // Notes on the sheet:
  //   fFULL SUBTRACTER
  //   bout
endmodule
