// Logisim project register.circ as structural Verilog: 2 circuits, main circuit main
module _4_itnp_i (
  input  [1:0] read1,
  input  [1:0] read2,
  input  [1:0] data_input,
  input  [3:0] write,
  input  in_5,
  output [3:0] read1_2,
  output [3:0] read2_2
);

  wire clock_out;

  main main_1 (
    .write(data_input), .data_input(write), .readport1(read1_2), .read1(read1), .readport2(read2_2),
    .read2(read2), .in_5(in_5), .in_6(clock_out));
  Clock clock (.out(clock_out));
endmodule

module main (
  input  [1:0] read1,
  input  [1:0] read2,
  input  [1:0] write,
  input  [3:0] data_input,
  input  in_5,
  input  in_6,
  output [3:0] readport1,
  output [3:0] readport2
);

  wire and_1_out, and_2_out, and_3_out, and_4_out, decoder_1_out0, decoder_1_out1, decoder_1_out2,
       decoder_1_out3;
  wire [3:0] register_1_q, register_2_q, register_3_q, register_4_q;

  Decoder #(.select(2)) decoder_1 (
    .out0(decoder_1_out0), .out1(decoder_1_out1), .out2(decoder_1_out2), .out3(decoder_1_out3), .sel(write));  // open: en
  and and_1 (and_1_out, decoder_1_out0, in_5);
  and and_2 (and_2_out, decoder_1_out1, in_5);
  and and_3 (and_3_out, decoder_1_out2, in_5);
  and and_4 (and_4_out, decoder_1_out3, in_5);
  Register #(.width(4)) register_1 (.D(data_input), .Q(register_1_q), .clk(in_6), .clr(and_1_out));  // open: en
  Register #(.width(4)) register_2 (.D(data_input), .Q(register_2_q), .clk(in_6), .clr(and_2_out));  // open: en
  Register #(.width(4)) register_3 (.D(data_input), .Q(register_3_q), .clk(in_6), .clr(and_3_out));  // open: en
  Register #(.width(4)) register_4 (.D(data_input), .Q(register_4_q), .clk(in_6), .clr(and_4_out));  // open: en
  Multiplexer #(.select(2), .width(4)) multiplexer_1 (
    .in0(register_1_q), .in1(register_2_q), .in2(register_3_q), .in3(register_4_q), .out(readport1),
    .sel(read1));  // open: en
  Multiplexer #(.select(2), .width(4)) multiplexer_2 (
    .in0(register_1_q), .in1(register_2_q), .in2(register_3_q), .in3(register_4_q), .out(readport2),
    .sel(read2));  // open: en
endmodule
