// Logisim project ALU RESGISTER.circ as structural Verilog: 2 circuits, main circuit main
module alu (
  input  [7:0] A,
  input  [7:0] B,
  input  sub,
  input  [2:0] op,
  output [7:0] out_5
);

  wire main_1_out_9, main_2_out_9, main_3_out_9, main_4_out_9, main_5_out_9, main_6_out_9, main_7_out_9,
       main_8_out_8;

  main main_1 (
    .in_4(A[0]), .in_5(B[0]), .in_6(main_8_out_8), .out_7(out_5[0]), .in_1(sub), .in_2(sub), .in_3(op),
    .out_9(main_1_out_9));  // open: out_8
  main main_2 (
    .in_4(A[1]), .in_5(B[1]), .in_6(1'b0), .out_7(out_5[1]), .in_1(1'b0), .in_2(main_1_out_9), .in_3(op),
    .out_9(main_2_out_9));  // open: out_8
  main main_3 (
    .in_4(A[2]), .in_5(B[2]), .in_6(1'b0), .out_7(out_5[2]), .in_1(1'b0), .in_2(main_2_out_9), .in_3(op),
    .out_9(main_3_out_9));  // open: out_8
  main main_4 (
    .in_4(A[3]), .in_5(B[3]), .in_6(1'b0), .out_7(out_5[3]), .in_1(sub), .in_2(main_3_out_9), .in_3(op),
    .out_9(main_4_out_9));  // open: out_8
  main main_5 (
    .in_4(A[4]), .in_5(B[4]), .in_6(1'b0), .out_7(out_5[4]), .in_1(sub), .in_2(main_4_out_9), .in_3(op),
    .out_9(main_5_out_9));  // open: out_8
  main main_6 (
    .in_4(A[5]), .in_5(B[5]), .in_6(1'b0), .out_7(out_5[5]), .in_1(sub), .in_2(main_5_out_9), .in_3(op),
    .out_9(main_6_out_9));  // open: out_8
  main main_7 (
    .in_4(A[6]), .in_5(B[6]), .in_6(1'b0), .out_7(out_5[6]), .in_1(sub), .in_2(main_6_out_9), .in_3(op),
    .out_9(main_7_out_9));  // open: out_8
  main main_8 (
    .in_4(A[7]), .in_5(B[7]), .in_6(1'b0), .out_7(out_5[7]), .in_1(sub), .in_2(main_7_out_9), .in_3(op),
    .out_8(main_8_out_8));  // open: out_9
endmodule

module main (
  input  in_1,
  input  in_2,
  input  [2:0] in_3,
  input  in_4,
  input  in_5,
  input  in_6,
  output out_7,
  output out_8,
  output out_9
);

  wire and_1_out, nor_1_out, or_1_out, xor_1_out, xor_2_out;

  xor xor_1 (xor_1_out, in_5, in_1);
  and and_1 (and_1_out, in_4, in_5);
  or or_1 (or_1_out, in_4, in_5);
  xor xor_2 (xor_2_out, in_4, in_5);
  nor nor_1 (nor_1_out, in_4, in_5);
  Adder #(.width(1)) adder_1 (.a(in_4), .b(xor_1_out), .out(out_8), .cin(in_2), .cout(out_9));
  Multiplexer #(.select(3)) multiplexer_1 (
    .in0(and_1_out), .in1(or_1_out), .in2(xor_2_out), .in3(nor_1_out), .in4(out_8), .in5(in_6), .out(out_7),
    .sel(in_3));  // open: in6, in7, en
endmodule
