// Logisim project full ader using muxxxxx.circ as structural Verilog: 2 circuits, main circuit main
module main (
  input  in_1,
  input  [1:0] in_2,
  output out_3,
  output out_4
);

  wire not_1_out;

  not not_1 (not_1_out, in_1);
  Multiplexer #(.select(2)) multiplexer_1 (
    .in0(in_1), .in1(not_1_out), .in2(not_1_out), .in3(in_1), .out(out_3), .sel(in_2));  // open: en
  Multiplexer #(.select(2)) multiplexer_2 (
    .in0(in_1), .in1(in_1), .in2(in_1), .in3(not_1_out), .out(out_4), .sel(in_2));  // open: en
endmodule

module New (
  input  in_1,
  input  [1:0] in_2,
  output out_3,
  output out_4
);

  main main_1 (.out_3(out_3), .out_4(out_4), .in_1(in_1), .in_2(in_2));
endmodule
