// Logisim project lab8_regFileAndAlu.circ as structural Verilog: 1 circuit, main circuit main
module main (
  input  in_1,
  input  [1:0] in_2
);

  wire and_1_out, and_2_out, and_3_out, and_4_out, clock_1_out, decoder_1_out0, decoder_1_out1,
       decoder_1_out2, decoder_1_out3;
  wire [3:0] register_1_q, register_3_q, register_4_q;
  wire [7:0] register_2_q;

  Decoder #(.select(2)) decoder_1 (
    .out0(decoder_1_out0), .out1(decoder_1_out1), .out2(decoder_1_out2), .out3(decoder_1_out3), .sel(in_2));  // open: en
  and and_1 (and_1_out, in_1, decoder_1_out0);
  and and_2 (and_2_out, in_1, decoder_1_out1);
  and and_3 (and_3_out, in_1, decoder_1_out2);
  and and_4 (and_4_out, decoder_1_out3, in_1);
  Clock clock_1 (.out(clock_1_out));
  Register #(.width(4)) register_1 (.en(and_1_out), .Q(register_1_q), .clk(clock_1_out));  // open: D, clr
  Register register_2 (.en(and_2_out), .Q(register_2_q), .clk(clock_1_out));  // open: D, clr
  Register #(.width(4)) register_3 (.en(and_3_out), .Q(register_3_q), .clk(clock_1_out));  // open: D, clr
  Register #(.width(4)) register_4 (.en(and_4_out), .Q(register_4_q), .clk(clock_1_out));  // open: D, clr
endmodule
