// Logisim project lab_7ALU.circ as structural Verilog: 1 circuit, main circuit main
module main (
  input  Cin,
  input  [3:0] A,
  input  [3:0] B,
  input  [1:0] S1S0,
  input  S2,
  output Cout,
  output Y
);

  wire main_1_p5, main_2_p4;

  // _4_bit_AU_main main_1: pin names not known; wires that end beside it: Cin, A, B, S1S0, main_1_p5, Cout
  // _4_bit_LU_main main_2: pin names not known; wires that end beside it: A, B, S1S0, main_2_p4
  Multiplexer multiplexer_1 (.in0(main_1_p5), .in1(main_2_p4), .out(Y), .sel(S2));  // open: en
endmodule
