// Logisim project parllal_adder.circ as structural Verilog: 2 circuits, main circuit main
module main (
  input  in_1,
  input  in_2,
  input  in_3,
  output sum,
  output carry
);

  wire and_1_out, and_2_out, xor_1_out;

  xor xor_1 (xor_1_out, in_1, in_2);
  and and_1 (and_1_out, in_2, in_1);
  xor xor_2 (sum, xor_1_out, in_3);
  and and_2 (and_2_out, in_3, xor_1_out);
  or or_1 (carry, and_2_out, and_1_out);
endmodule

module fghfg (
  input  in_1,
  input  [3:0] in_2,
  input  [3:0] in_3,
  output [3:0] out_4,
  output out_5
);

  wire main_2_carry;

  main main_1 (.in_1(in_1), .in_2(in_2[0]), .in_3(in_3[0]), .sum(out_4[0]), .carry(in_2[1]));
  main main_2 (.in_1(in_2[1]), .in_2(in_2[1]), .in_3(in_3[1]), .sum(out_4[1]), .carry(main_2_carry));
  main main_3 (.in_1(main_2_carry), .in_2(in_2[2]), .in_3(in_2[2]), .sum(out_4[2]), .carry(in_2[3]));
  main main_4 (.in_1(in_2[3]), .in_2(in_2[3]), .in_3(in_3[3]), .sum(out_4[3]), .carry(out_5));

  assign in_3[2] = in_2[2];
endmodule
